// Logisim project control-logic.circ as structural Verilog: 1 circuit, main circuit control_logic
module control_logic (
  input  [31:0] Instruction,
  input  BrEq,
  input  BrLt,
  output PCSel,
  output RegWEn,
  output [2:0] ImmSel,
  output BrUn,
  output ASel,
  output BSel,
  output [3:0] ALUSel,
  output MemWEn,
  output [1:0] WBSel
);

  wire and_20_out, and_21_out, and_22_out, and_23_out, and_24_out, and_25_out, auipc, btype, comparator_1_eq,
       comparator_2_eq, comparator_3_eq, comparator_4_eq, comparator_9_eq, comparator_10_eq,
       comparator_11_eq, comparator_12_eq, comparator_13_eq, comparator_14_eq, comparator_17_eq,
       comparator_18_eq, comparator_19_eq, comparator_20_eq, comparator_21_eq, comparator_22_eq,
       comparator_23_eq, comparator_26_eq, comparator_27_eq, comparator_28_eq, comparator_29_eq,
       comparator_31_eq, comparator_32_eq, isAdd, isAnd, isBeq, isBge, isBgeu, isBlt, isBltu, isBne, isMul,
       isMulh, isMulhu, isOr, isSll, isSlt, isSra, isSrl, isSub, isXor, itype, jal, jalr, load, lui,
       multiplexer_1_out, multiplexer_3_out, multiplexer_4_out, multiplexer_5_out, multiplexer_7_out,
       multiplexer_9_out, multiplexer_10_out, multiplexer_11_out, multiplexer_14_out, multiplexer_16_out,
       multiplexer_17_out, multiplexer_18_out, multiplexer_21_out, multiplexer_23_out, multiplexer_24_out,
       multiplexer_25_out, multiplexer_28_out, multiplexer_30_out, multiplexer_31_out, multiplexer_32_out,
       multiplexer_35_out, multiplexer_38_out, multiplexer_39_out, multiplexer_40_out, multiplexer_44_out,
       multiplexer_46_out, multiplexer_47_out, multiplexer_48_out, multiplexer_51_out, multiplexer_53_out,
       multiplexer_54_out, multiplexer_55_out, not_1_out, not_2_out, not_3_out, not_4_out, not_5_out,
       or_1_out, or_2_out, or_3_out, or_4_out, or_5_out, or_6_out, or_7_out, or_8_out, rtype, store;
  wire [1:0] multiplexer_6_out, multiplexer_12_out, multiplexer_19_out, multiplexer_26_out,
       multiplexer_33_out, multiplexer_41_out, multiplexer_49_out, multiplexer_56_out;
  wire [2:0] multiplexer_2_out, multiplexer_8_out, multiplexer_15_out, multiplexer_22_out,
       multiplexer_29_out, multiplexer_36_out, multiplexer_45_out, multiplexer_52_out;
  wire [3:0] multiplexer_13_out, multiplexer_20_out, multiplexer_27_out, multiplexer_34_out,
       multiplexer_37_out, multiplexer_42_out, multiplexer_43_out, multiplexer_50_out, multiplexer_57_out,
       multiplexer_58_out, multiplexer_65_out;
  wire [15:0] rom_1_data;

  or or_1 (or_1_out, rtype, itype);
  or or_2 (or_2_out, rtype, itype);
  Comparator #(.width(3)) comparator_1 (.a(Instruction[14:12]), .b(3'b000), .eq(comparator_1_eq));  // open: gt, lt
  or or_3 (or_3_out, rtype, itype, lui, load, store);
  Comparator #(.width(7)) comparator_2 (.a(Instruction[31:25]), .b(7'b0100000), .eq(comparator_2_eq));  // open: gt, lt
  Comparator #(.width(3)) comparator_3 (.a(Instruction[14:12]), .b(3'b111), .eq(comparator_3_eq));  // open: gt, lt
  Comparator #(.width(3)) comparator_4 (.a(Instruction[14:12]), .b(3'b110), .eq(comparator_4_eq));  // open: gt, lt
  Comparator #(.width(7)) comparator_5 (.a(Instruction[6:0]), .b(7'b0010011), .eq(itype));  // open: gt, lt
  Comparator #(.width(7)) comparator_6 (.a(Instruction[6:0]), .b(7'b0110011), .eq(rtype));  // open: gt, lt
  and and_1 (isAdd, comparator_1_eq, or_3_out);
  and and_2 (isSub, comparator_2_eq, rtype);
  and and_3 (isAnd, comparator_3_eq, or_1_out);
  and and_4 (isOr, comparator_4_eq, or_2_out);
  ROM #(.addrWidth(6), .dataWidth(16)) rom_1 (.data(rom_1_data));  // open: addr
  Comparator #(.width(7)) comparator_7 (.a(Instruction[6:0]), .b(7'b1100011), .eq(btype));  // open: gt, lt
  Comparator #(.width(7)) comparator_8 (.a(Instruction[6:0]), .b(7'b0110111), .eq(lui));  // open: gt, lt
  Comparator #(.width(3)) comparator_9 (.a(Instruction[14:12]), .b(3'b100), .eq(comparator_9_eq));  // open: gt, lt
  or or_4 (or_4_out, rtype, itype);
  Comparator #(.width(3)) comparator_10 (.a(Instruction[14:12]), .b(3'b001), .eq(comparator_10_eq));  // open: gt, lt
  or or_5 (or_5_out, rtype, itype);
  Comparator #(.width(3)) comparator_11 (.a(Instruction[14:12]), .b(3'b101), .eq(comparator_11_eq));  // open: gt, lt
  Comparator #(.width(7)) comparator_12 (.a(Instruction[31:25]), .b({7{1'b0}}), .eq(comparator_12_eq));  // open: gt, lt
  or or_6 (or_6_out, rtype, itype);
  Comparator #(.width(3)) comparator_13 (.a(Instruction[14:12]), .b(3'b101), .eq(comparator_13_eq));  // open: gt, lt
  Comparator #(.width(7)) comparator_14 (
    .a(Instruction[31:25]), .b(7'b0100000), .eq(comparator_14_eq));  // open: gt, lt
  or or_7 (or_7_out, rtype, itype);
  and and_5 (isXor, comparator_9_eq, or_4_out);
  and and_6 (isSll, comparator_10_eq, or_5_out);
  and and_7 (isSrl, comparator_11_eq, comparator_12_eq, or_6_out);
  and and_8 (isSra, comparator_13_eq, comparator_14_eq, or_7_out);
  Comparator #(.width(7)) comparator_15 (.a(Instruction[6:0]), .b(7'b0000011), .eq(load));  // open: gt, lt
  Comparator #(.width(7)) comparator_16 (.a(Instruction[6:0]), .b(7'b0100011), .eq(store));  // open: gt, lt
  Comparator #(.width(3)) comparator_17 (.a(Instruction[14:12]), .b(3'b010), .eq(comparator_17_eq));  // open: gt, lt
  or or_8 (or_8_out, rtype, itype);
  Comparator #(.width(3)) comparator_18 (.a(Instruction[14:12]), .b(3'b000), .eq(comparator_18_eq));  // open: gt, lt
  Comparator #(.width(7)) comparator_19 (
    .a(Instruction[31:25]), .b(7'b0000001), .eq(comparator_19_eq));  // open: gt, lt
  Comparator #(.width(3)) comparator_20 (.a(Instruction[14:12]), .b(3'b001), .eq(comparator_20_eq));  // open: gt, lt
  Comparator #(.width(7)) comparator_21 (
    .a(Instruction[31:25]), .b(7'b0000001), .eq(comparator_21_eq));  // open: gt, lt
  Comparator #(.width(3)) comparator_22 (.a(Instruction[14:12]), .b(3'b011), .eq(comparator_22_eq));  // open: gt, lt
  Comparator #(.width(7)) comparator_23 (
    .a(Instruction[31:25]), .b(7'b0000001), .eq(comparator_23_eq));  // open: gt, lt
  Multiplexer multiplexer_1 (.in0(1'b0), .in1(1'b1), .out(multiplexer_1_out), .sel(itype));
  Multiplexer #(.width(3)) multiplexer_2 (.in0(3'b000), .in1(3'b000), .out(multiplexer_2_out), .sel(itype));
  Multiplexer multiplexer_3 (.in0(1'b0), .in1(1'b0), .out(multiplexer_3_out), .sel(itype));
  Multiplexer multiplexer_4 (.in0(1'b0), .in1(1'b0), .out(multiplexer_4_out), .sel(itype));
  Multiplexer multiplexer_5 (.in0(1'b0), .in1(1'b0), .out(multiplexer_5_out), .sel(itype));
  Multiplexer #(.width(2)) multiplexer_6 (.in0(2'b00), .in1(2'b00), .out(multiplexer_6_out), .sel(itype));
  Multiplexer multiplexer_7 (.in0(multiplexer_1_out), .in1(1'b1), .out(multiplexer_7_out), .sel(rtype));
  Multiplexer #(.width(3)) multiplexer_8 (.in0(multiplexer_2_out), .in1(3'b000), .out(multiplexer_8_out), .sel(rtype));
  Multiplexer multiplexer_9 (.in0(multiplexer_3_out), .in1(1'b0), .out(multiplexer_9_out), .sel(rtype));
  Multiplexer multiplexer_10 (.in0(multiplexer_4_out), .in1(1'b1), .out(multiplexer_10_out), .sel(rtype));
  Multiplexer multiplexer_11 (.in0(multiplexer_5_out), .in1(1'b0), .out(multiplexer_11_out), .sel(rtype));
  Multiplexer #(.width(2)) multiplexer_12 (.in0(multiplexer_6_out), .in1(2'b00), .out(multiplexer_12_out), .sel(rtype));
  Multiplexer #(.width(4)) multiplexer_13 (.in0(4'b0000), .in1(4'b0000), .out(multiplexer_13_out), .sel(isAdd));
  Comparator #(.width(7)) comparator_24 (.a(Instruction[6:0]), .b(7'b1101111), .eq(jal));  // open: gt, lt
  and and_9 (isSlt, comparator_17_eq, or_8_out);
  and and_10 (isMul, comparator_18_eq, comparator_19_eq, rtype);
  and and_11 (isMulh, comparator_20_eq, comparator_21_eq, rtype);
  and and_12 (isMulhu, comparator_22_eq, comparator_23_eq, rtype);
  Multiplexer multiplexer_14 (.in0(multiplexer_7_out), .in1(1'b0), .out(multiplexer_14_out), .sel(btype));
  Multiplexer #(.width(3)) multiplexer_15 (
    .in0(multiplexer_8_out), .in1(3'b010), .out(multiplexer_15_out), .sel(btype));
  Multiplexer multiplexer_16 (.in0(multiplexer_9_out), .in1(1'b1), .out(multiplexer_16_out), .sel(btype));
  Multiplexer multiplexer_17 (.in0(multiplexer_10_out), .in1(1'b0), .out(multiplexer_17_out), .sel(btype));
  Multiplexer multiplexer_18 (.in0(multiplexer_11_out), .in1(1'b0), .out(multiplexer_18_out), .sel(btype));
  Multiplexer #(.width(2)) multiplexer_19 (
    .in0(multiplexer_12_out), .in1(2'b00), .out(multiplexer_19_out), .sel(btype));
  Multiplexer #(.width(4)) multiplexer_20 (
    .in0(multiplexer_13_out), .in1(4'b1100), .out(multiplexer_20_out), .sel(isSub));
  Multiplexer multiplexer_21 (.in0(multiplexer_14_out), .in1(1'b1), .out(multiplexer_21_out), .sel(lui));
  Multiplexer #(.width(3)) multiplexer_22 (.in0(multiplexer_15_out), .in1(3'b011), .out(multiplexer_22_out), .sel(lui));
  Multiplexer multiplexer_23 (.in0(multiplexer_16_out), .in1(1'b0), .out(multiplexer_23_out), .sel(lui));
  Multiplexer multiplexer_24 (.in0(multiplexer_17_out), .in1(1'b0), .out(multiplexer_24_out), .sel(lui));
  Multiplexer multiplexer_25 (.in0(multiplexer_18_out), .in1(1'b0), .out(multiplexer_25_out), .sel(lui));
  Multiplexer #(.width(2)) multiplexer_26 (.in0(multiplexer_19_out), .in1(2'b00), .out(multiplexer_26_out), .sel(lui));
  Multiplexer #(.width(4)) multiplexer_27 (
    .in0(multiplexer_20_out), .in1(4'b0111), .out(multiplexer_27_out), .sel(isAnd));
  Multiplexer multiplexer_28 (.in0(multiplexer_21_out), .in1(1'b1), .out(multiplexer_28_out), .sel(load));
  Multiplexer #(.width(3)) multiplexer_29 (
    .in0(multiplexer_22_out), .in1(3'b000), .out(multiplexer_29_out), .sel(load));
  Multiplexer multiplexer_30 (.in0(multiplexer_23_out), .in1(1'b0), .out(multiplexer_30_out), .sel(load));
  Multiplexer multiplexer_31 (.in0(multiplexer_24_out), .in1(1'b0), .out(multiplexer_31_out), .sel(load));
  Multiplexer multiplexer_32 (.in0(multiplexer_25_out), .in1(1'b0), .out(multiplexer_32_out), .sel(load));
  Multiplexer #(.width(2)) multiplexer_33 (.in0(multiplexer_26_out), .in1(2'b01), .out(multiplexer_33_out), .sel(load));
  Multiplexer #(.width(4)) multiplexer_34 (
    .in0(multiplexer_27_out), .in1(4'b0110), .out(multiplexer_34_out), .sel(isOr));
  Comparator #(.width(7)) comparator_25 (.a(Instruction[6:0]), .b(7'b1100111), .eq(jalr));  // open: gt, lt
  Multiplexer multiplexer_35 (.in0(multiplexer_28_out), .in1(1'b0), .out(multiplexer_35_out), .sel(store));
  Multiplexer #(.width(3)) multiplexer_36 (
    .in0(multiplexer_29_out), .in1(3'b001), .out(multiplexer_36_out), .sel(store));
  Multiplexer #(.width(4)) multiplexer_37 (
    .in0(multiplexer_34_out), .in1(4'b0100), .out(multiplexer_37_out), .sel(isXor));
  Comparator #(.width(3)) comparator_26 (.a(Instruction[14:12]), .b(3'b000), .eq(comparator_26_eq));  // open: gt, lt
  Comparator #(.width(3)) comparator_27 (.a(Instruction[14:12]), .b(3'b101), .eq(comparator_27_eq));  // open: gt, lt
  Comparator #(.width(3)) comparator_28 (.a(Instruction[14:12]), .b(3'b111), .eq(comparator_28_eq));  // open: gt, lt
  Comparator #(.width(3)) comparator_29 (.a(Instruction[14:12]), .b(3'b100), .eq(comparator_29_eq));  // open: gt, lt
  Multiplexer multiplexer_38 (.in0(multiplexer_30_out), .in1(1'b0), .out(multiplexer_38_out), .sel(store));
  Multiplexer multiplexer_39 (.in0(multiplexer_31_out), .in1(1'b0), .out(multiplexer_39_out), .sel(store));
  Multiplexer multiplexer_40 (.in0(multiplexer_32_out), .in1(1'b1), .out(multiplexer_40_out), .sel(store));
  Multiplexer #(.width(2)) multiplexer_41 (
    .in0(multiplexer_33_out), .in1(2'b10), .out(multiplexer_41_out), .sel(store));
  Multiplexer #(.width(4)) multiplexer_42 (
    .in0(multiplexer_37_out), .in1(4'b0001), .out(multiplexer_42_out), .sel(isSll));
  Multiplexer #(.width(4)) multiplexer_43 (
    .in0(multiplexer_42_out), .in1(4'b0101), .out(multiplexer_43_out), .sel(isSrl));
  and and_13 (isBeq, comparator_26_eq, btype);
  and and_14 (isBge, comparator_27_eq, btype);
  and and_15 (isBgeu, comparator_28_eq, btype);
  and and_16 (isBlt, comparator_29_eq, btype);
  Multiplexer multiplexer_44 (.in0(multiplexer_35_out), .in1(1'b1), .out(multiplexer_44_out), .sel(jal));
  Multiplexer #(.width(3)) multiplexer_45 (.in0(multiplexer_36_out), .in1(3'b100), .out(multiplexer_45_out), .sel(jal));
  Multiplexer multiplexer_46 (.in0(multiplexer_38_out), .in1(1'b1), .out(multiplexer_46_out), .sel(jal));
  Multiplexer multiplexer_47 (.in0(multiplexer_39_out), .in1(1'b0), .out(multiplexer_47_out), .sel(jal));
  Multiplexer multiplexer_48 (.in0(multiplexer_40_out), .in1(1'b0), .out(multiplexer_48_out), .sel(jal));
  Multiplexer #(.width(2)) multiplexer_49 (.in0(multiplexer_41_out), .in1(2'b11), .out(multiplexer_49_out), .sel(jal));
  Multiplexer #(.width(4)) multiplexer_50 (
    .in0(multiplexer_43_out), .in1(4'b1101), .out(multiplexer_50_out), .sel(isSra));
  Multiplexer multiplexer_51 (.in0(multiplexer_44_out), .in1(1'b1), .out(multiplexer_51_out), .sel(jalr));
  Multiplexer #(.width(3)) multiplexer_52 (
    .in0(multiplexer_45_out), .in1(3'b000), .out(multiplexer_52_out), .sel(jalr));
  Multiplexer multiplexer_53 (.in0(multiplexer_46_out), .in1(1'b0), .out(multiplexer_53_out), .sel(jalr));
  Multiplexer multiplexer_54 (.in0(multiplexer_47_out), .in1(1'b0), .out(multiplexer_54_out), .sel(jalr));
  Multiplexer multiplexer_55 (.in0(multiplexer_48_out), .in1(1'b0), .out(multiplexer_55_out), .sel(jalr));
  Multiplexer #(.width(2)) multiplexer_56 (.in0(multiplexer_49_out), .in1(2'b11), .out(multiplexer_56_out), .sel(jalr));
  Multiplexer #(.width(4)) multiplexer_57 (
    .in0(multiplexer_50_out), .in1(4'b0010), .out(multiplexer_57_out), .sel(isSlt));
  Multiplexer #(.width(4)) multiplexer_58 (
    .in0(multiplexer_57_out), .in1(4'b1000), .out(multiplexer_58_out), .sel(isMul));
  Comparator #(.width(7)) comparator_30 (.a(Instruction[6:0]), .b(7'b0010111), .eq(auipc));  // open: gt, lt
  Multiplexer multiplexer_59 (.in0(multiplexer_51_out), .in1(1'b1), .out(RegWEn), .sel(auipc));
  Multiplexer #(.width(3)) multiplexer_60 (.in0(multiplexer_52_out), .in1(3'b011), .out(ImmSel), .sel(auipc));
  Multiplexer multiplexer_61 (.in0(multiplexer_53_out), .in1(1'b1), .out(ASel), .sel(auipc));
  Multiplexer multiplexer_62 (.in0(multiplexer_54_out), .in1(1'b0), .out(BSel), .sel(auipc));
  Multiplexer multiplexer_63 (.in0(multiplexer_55_out), .in1(1'b0), .out(MemWEn), .sel(auipc));
  Multiplexer #(.width(2)) multiplexer_64 (.in0(multiplexer_56_out), .in1(2'b00), .out(WBSel), .sel(auipc));
  Multiplexer #(.width(4)) multiplexer_65 (
    .in0(multiplexer_58_out), .in1(4'b1001), .out(multiplexer_65_out), .sel(isMulh));
  Multiplexer #(.width(4)) multiplexer_66 (.in0(multiplexer_65_out), .in1(4'b1011), .out(ALUSel), .sel(isMulhu));
  Comparator #(.width(3)) comparator_31 (.a(Instruction[14:12]), .b(3'b110), .eq(comparator_31_eq));  // open: gt, lt
  Comparator #(.width(3)) comparator_32 (.a(Instruction[14:12]), .b(3'b001), .eq(comparator_32_eq));  // open: gt, lt
  and and_17 (isBltu, comparator_31_eq, btype);
  and and_18 (isBne, comparator_32_eq, btype);
  not not_1 (not_1_out, isBge);
  not not_2 (not_2_out, isBlt);
  not not_3 (not_3_out, BrLt);
  not not_4 (not_4_out, BrEq);
  not not_5 (not_5_out, BrLt);
  and and_19 (BrUn, not_1_out, isBgeu, isBltu, not_2_out);
  and and_20 (and_20_out, isBeq, BrEq);
  and and_21 (and_21_out, isBge, not_3_out);
  and and_22 (and_22_out, isBlt, BrLt);
  and and_23 (and_23_out, isBne, not_4_out);
  and and_24 (and_24_out, isBltu, BrLt);
  and and_25 (and_25_out, isBgeu, not_5_out);
  or or_9 (PCSel, jalr, and_20_out, and_21_out, and_22_out, and_23_out, and_24_out, and_25_out, jal);

  // Other names for the same wires on the sheet: opcode[6:0] = Instruction[6:0]; rd[4:0] = Instruction[11:7];
  //   funct3[2:0] = Instruction[14:12]; rs1[4:0] = Instruction[19:15]; rs2[4:0] = Instruction[24:20];
  //   funct7[6:0] = Instruction[31:25]

  // Notes on the sheet:
  //   INPUTS to your circuit
  //   Connect ROM Input here ->
  //   ROM FOR CONTROL LOGIC
  //   DON'T CHANGE THE LOCATIONS OF THE INPUTS AND OUTPUTS!
  //   This is only if you choose to do the ROM option
  //   CONNECT
  //   WIRE
  //   TO
  //   USE
  //   ROM
  //   OUTPUT from your circuit
  //   Reminder: If using ROM, use combinational logic for PCSel
endmodule
