// Logisim project cpu.circ as structural Verilog: 1 circuit, main circuit cpu
module cpu (
  input  clk,
  input  [31:0] Instruction,
  input  [31:0] MemReadData,
  output [31:0] MemAddress,
  output [31:0] ProgramCounter,
  output [31:0] ra,
  output [31:0] sp,
  output [31:0] t0,
  output [31:0] t1,
  output [31:0] t2,
  output [31:0] s0,
  output [31:0] s1,
  output [31:0] a0,
  output [3:0] MemWriteMask,
  output [31:0] MemWriteData
);

  wire ASel, BrEq, BrLt, BrUn, BSel, lui, MemWEn, PCSel, RegWEn;
  wire [1:0] WBSel;
  wire [2:0] funct3, ImmSel;
  wire [3:0] ALUSel;
  wire [6:0] funct7;
  wire [24:0] Instruction2;
  wire [31:0] adder_1_out, adder_2_out, DataToReg, Immediate, multiplexer_1_out, multiplexer_2_out,
       multiplexer_3_out, multiplexer_4_out, multiplexer_5_out, ProgramCounter2, rd1, rd2, WriteData;

  Adder #(.width(32)) adder_1 (.a(ProgramCounter), .b(32'h4), .out(adder_1_out));  // open: cin, cout
  Multiplexer #(.width(32)) multiplexer_1 (.in0(adder_1_out), .in1(MemAddress), .out(multiplexer_1_out), .sel(PCSel));
  Comparator #(.width(7)) comparator_1 (.a(Instruction2[6:0]), .b(7'b0110111), .eq(lui));  // open: gt, lt
  Register #(.width(32)) PC (.D(multiplexer_1_out), .clk(clk), .Q(ProgramCounter));  // open: en, clr
  Register #(.width(32)) register_1 (.D(ProgramCounter), .clk(clk), .Q(ProgramCounter2));  // open: en, clr
  Multiplexer #(.width(32)) multiplexer_2 (.in0(Instruction), .in1(32'h13), .out(multiplexer_2_out), .sel(PCSel));
  Register #(.width(32)) register_2 (
    .D(multiplexer_2_out), .clk(clk), .Q({funct7, Instruction2[24:15], funct3, Instruction2[11:0]}));  // open: en, clr
  control_logic control_logic_1 (
    .Instruction({funct7, Instruction2[24:15], funct3, Instruction2[11:0]}), .BrEq(BrEq), .BrLt(BrLt),
    .PCSel(PCSel), .RegWEn(RegWEn), .ImmSel(ImmSel), .BrUn(BrUn), .ASel(ASel), .BSel(BSel), .ALUSel(ALUSel),
    .MemWEn(MemWEn), .WBSel(WBSel));
  imm_gen imm_gen_1 (
    .Instruction({funct7, Instruction2[24:15], funct3, Instruction2[11:0]}), .ImmSel(ImmSel),
    .Immediate(Immediate));
  branch_comp branch_comp_1 (.BrData1(rd1), .BrData2(rd2), .BrUn(BrUn), .BrEq(BrEq), .BrLt(BrLt));
  regfile regfile_1 (
    .ReadIndex1(Instruction2[19:15]), .ReadIndex2(Instruction2[24:20]), .WriteIndex(Instruction2[11:7]),
    .WriteData(MemAddress), .RegWEn(RegWEn), .clk(clk), .ra(ra), .sp(sp), .t0(t0), .t1(t1), .t2(t2), .s0(s0),
    .s1(s1), .a0(a0), .ReadData1(rd1), .ReadData2(rd2));
  Multiplexer #(.enable("true"), .width(32)) multiplexer_3 (
    .in0(rd1), .in1({32{1'b0}}), .out(multiplexer_3_out), .sel(lui));  // open: en
  Multiplexer #(.enable("true"), .width(32)) multiplexer_4 (
    .in0(multiplexer_3_out), .in1(ProgramCounter2), .out(multiplexer_4_out), .sel(ASel));  // open: en
  Multiplexer #(.enable("true"), .width(32)) multiplexer_5 (
    .in0(Immediate), .in1(rd2), .out(multiplexer_5_out), .sel(BSel));  // open: en
  alu alu_1 (.A(multiplexer_4_out), .B(multiplexer_5_out), .ALUSel(ALUSel), .ALUResult(MemAddress));
  Adder #(.width(32)) adder_2 (.a(ProgramCounter2), .b(32'h4), .out(adder_2_out));  // open: cin, cout
  Multiplexer #(.enable("true"), .select(2), .width(32)) multiplexer_6 (
    .in0(DataToReg), .in1(MemAddress), .in2(adder_2_out), .in3(Immediate), .out(WriteData), .sel(WBSel));  // open: en
  partial_store partial_store_1 (
    .Instruction({funct7, Instruction2[24:15], funct3, Instruction2[11:0]}), .MemAddress(MemAddress),
    .DataFromReg(rd2), .MemWEn(MemWEn), .MemWriteMask(MemWriteMask), .DataToMem(MemWriteData));
  partial_load partial_load_1 (
    .Instruction({funct7, Instruction2[24:15], funct3, Instruction2[11:0]}), .MemAddress(MemAddress),
    .DataFromMem(MemReadData), .DataToReg(DataToReg));

  // Other names for the same wires on the sheet: ALUResult[31:0] = MemAddress; opcode[6:0] = Instruction2[6:0];
  //   rd[4:0] = Instruction2[11:7]; Instruction2 (some bits) = {funct7, funct3}; rs1[4:0] = Instruction2[19:15];
  //   rs2[4:0] = Instruction2[24:20]

  // Notes on the sheet:
  //   To IMEM
  //   IMEM (do **NOT** move this)
  //   From IMEM
  //   Inputs/Outputs for testing. Do **NOT** move these.
  //   It is OK to move the PC, RegFile, ALU, MEM, Branch Comp, Imm Gen, Partial Load, Partial Store and Control Logic to wherever is most convenient for you when constructing your CPU, and to delete this text
  //   To DMEM
  //   DMEM (do **NOT** move this)
  //   From DMEM
endmodule
